# Fritzing sketch fish_feed (saved by Fritzing 0.9.3b)
breadboards: 1

parts:
  DHT1 = DHT22_Humidity_and_Temperature_Sensor
  Part1 = Photon
  R1 = Resistor [tolerance=±5% resistance=220 package="0402 [SMD]"]
  Raspberry_Pi_1 = Raspberry Pi 3 [part_number=RPI-3-V1.2]
  U1 = TRANSCHIPTC5747 [package=camera_sfv24r-2st_2]  # not connected
  J1 = Basic Servo

nets:
  N1: DHT1.connector1, Part1.VIN, Part1.D3, R1.Pin_0
  N2: DHT1.connector2, Part1.D0, R1.Pin_1
  N3: DHT1.connector4, Part1.GND
  N4: Raspberry_Pi_1.GPIO18, J1.pulse
  GND: Raspberry_Pi_1.GND, J1.gnd
  5V: Raspberry_Pi_1.5V, J1.vcc
